# Fritzing sketch Weather Station ESP8266 on Breadboard (saved by Fritzing 0.9.3b)
breadboards: 2

parts:
  U1 = NodeMCU V3.0
  OLED1 = OLED 128x64 I2C Monochrome Display
  Part1 = LC Studio SD Card Module  # not connected
  DHT1 = DHT22 Humidity and Temperature Sensor
  R1 = Photocell (LDR) [package=THT]
  R2 = Resistor [tolerance=±5% resistance=220 package=THT]

nets:
  N1: U1.D1, OLED1.SCK
  N2: U1.D2, OLED1.SDA
  N3: U1.D4, DHT1.DATA
  VDD: U1.3V3, OLED1.VDD, DHT1.VDD, R1.pin_1
  GND: U1.GND#6, U1.GND#13, U1.GND#16, U1.GND#33, OLED1.GND, DHT1.GND
  N4: U1.GND#41, R2.Pin_0
  N5: U1.A0, R1.pin_0, R2.Pin_1

custom parts:
  NodeMCU V3.0: ESP8266 based NodeMCU
  LC Studio SD Card Module: The LC Studio SD card module serves as an interface to an SD card. The module works at 3.3 volts and 5 volts. The SPI (Serial Peripheral Interface) protocol is used for communicating with the module.
